// Logisim project batalhaNaval.circ as structural Verilog: 9 circuits, main circuit main
module main (
);

  wire and_1_out, and_2_out, button_1_out, comparador_1_out_9, comparador_2_out_9, decodificador_1_saidas1,
       decodificador_1_saidas2, decodificador_1_saidas3, decodificador_1_saidas4, dipswitch_1_p1,
       dipswitch_1_p2, dipswitch_1_p3, dipswitch_1_p4, dipswitch_2_sw1, dipswitch_2_sw2, dipswitch_2_sw3,
       dipswitch_2_sw4, dipswitch_2_sw5, dipswitch_2_sw6, dipswitch_2_sw7, dipswitch_2_sw8, latch_1_acertou,
       latch_1_errou, not_1_out, or_1_out;

  Button button_1 (.out(button_1_out));
  // DipSwitch dipswitch_1: pin names not known; wires that end beside it: dipswitch_1_p1, dipswitch_1_p2, dipswitch_1_p3, dipswitch_1_p4
  DipSwitch dipswitch_2 (
    .sw1(dipswitch_2_sw1), .sw2(dipswitch_2_sw2), .sw3(dipswitch_2_sw3), .sw4(dipswitch_2_sw4),
    .sw5(dipswitch_2_sw5), .sw6(dipswitch_2_sw6), .sw7(dipswitch_2_sw7), .sw8(dipswitch_2_sw8));
  Decodificador decodificador_1 (
    .A(dipswitch_1_p1), .B(dipswitch_1_p2), .C(dipswitch_1_p3), .D(dipswitch_1_p4),
    .SaidaS1(decodificador_1_saidas1), .SaidaS2(decodificador_1_saidas2), .SaidaS3(decodificador_1_saidas3),
    .SaidaS4(decodificador_1_saidas4));
  Comparador comparador_1 (
    .Bit0DoNavio(dipswitch_2_sw1), .Bit0DoTIro(decodificador_1_saidas1), .Bit1DoNavio(dipswitch_2_sw2),
    .Bit1DoTIro(decodificador_1_saidas2), .Bit2DoNavio(dipswitch_2_sw3),
    .Bit2DoTIro(decodificador_1_saidas3), .Bit3DoNavio(dipswitch_2_sw4),
    .Bit3DoTIro(decodificador_1_saidas4), .out_9(comparador_1_out_9));
  Comparador comparador_2 (
    .Bit0DoNavio(dipswitch_2_sw5), .Bit0DoTIro(decodificador_1_saidas1), .Bit1DoNavio(dipswitch_2_sw6),
    .Bit1DoTIro(decodificador_1_saidas2), .Bit2DoNavio(dipswitch_2_sw7),
    .Bit2DoTIro(decodificador_1_saidas3), .Bit3DoNavio(decodificador_1_saidas4),
    .Bit3DoTIro(dipswitch_2_sw8), .out_9(comparador_2_out_9));
  or or_1 (or_1_out, comparador_1_out_9, comparador_2_out_9);
  not not_1 (not_1_out, or_1_out);
  and and_1 (and_1_out, not_1_out, button_1_out);
  and and_2 (and_2_out, button_1_out, or_1_out);
  Latch latch_1 (.R(and_1_out), .S(and_2_out), .Acertou(latch_1_acertou), .Errou(latch_1_errou));
  LED led_1 (.in(latch_1_acertou));
  LED led_2 (.in(latch_1_errou));
endmodule

module S1 (
  input  A,
  input  B,
  input  C,
  input  D,
  output out_5
);

  wire and_1_out, and_2_out, and_3_out, and_4_out, not_1_out, not_2_out, not_3_out, not_4_out, not_5_out;

  not not_1 (not_1_out, A);
  not not_2 (not_2_out, B);
  not not_3 (not_3_out, D);
  not not_4 (not_4_out, A);
  and and_1 (and_1_out, not_4_out, not_5_out);
  not not_5 (not_5_out, B);
  and and_2 (and_2_out, not_1_out, D);
  and and_3 (and_3_out, not_2_out, C, not_3_out);
  and and_4 (and_4_out, B, C, D);
  or or_1 (out_5, and_1_out, and_2_out, and_3_out, and_4_out);
endmodule

module S2 (
  input  A,
  input  B,
  input  C,
  input  D,
  output out_5
);

  wire and_1_out, and_2_out, and_3_out, not_1_out, not_2_out, not_3_out, not_4_out;

  not not_1 (not_1_out, A);
  not not_2 (not_2_out, B);
  not not_3 (not_3_out, C);
  not not_4 (not_4_out, D);
  and and_1 (and_1_out, A, not_2_out, C);
  and and_2 (and_2_out, not_2_out, not_3_out, D);
  and and_3 (and_3_out, not_1_out, not_4_out);
  or or_1 (out_5, and_1_out, and_2_out, and_3_out);
endmodule

module S3 (
  input  A,
  input  B,
  input  C,
  input  D,
  output out_5
);

  wire and_1_out, and_2_out, and_3_out, and_4_out, and_5_out, not_1_out, not_2_out, not_3_out, not_4_out,
       not_5_out, not_6_out, not_7_out, not_8_out, not_9_out;

  not not_1 (not_1_out, A);
  not not_2 (not_2_out, B);
  not not_3 (not_3_out, C);
  not not_4 (not_4_out, D);
  not not_5 (not_5_out, B);
  not not_6 (not_6_out, C);
  not not_7 (not_7_out, A);
  not not_8 (not_8_out, B);
  not not_9 (not_9_out, C);
  and and_1 (and_1_out, not_1_out, B, C);
  and and_2 (and_2_out, not_2_out, not_3_out, not_4_out);
  and and_3 (and_3_out, not_5_out, C, D);
  and and_4 (and_4_out, A, B, not_6_out, D);
  and and_5 (and_5_out, not_7_out, not_8_out, not_9_out);
  or or_1 (out_5, and_1_out, and_2_out, and_3_out, and_4_out, and_5_out);
endmodule

module S4 (
  input  A,
  input  B,
  input  C,
  input  D,
  output out_5
);

  wire and_1_out, and_2_out, and_3_out, and_4_out, and_5_out, not_1_out, not_2_out, not_3_out, not_4_out,
       not_5_out;

  not not_1 (not_1_out, A);
  not not_2 (not_2_out, B);
  not not_3 (not_3_out, A);
  not not_4 (not_4_out, D);
  not not_5 (not_5_out, D);
  and and_1 (and_1_out, not_1_out, not_2_out);
  and and_2 (and_2_out, and_1_out, C);
  and and_3 (and_3_out, A, B, D);
  and and_4 (and_4_out, B, C, not_5_out);
  and and_5 (and_5_out, not_3_out, not_4_out);
  or or_1 (out_5, and_5_out, and_2_out, and_3_out, and_4_out);
endmodule

module ComparadorDeBit (
  input  BitDoNavio,
  input  BitDoTiro,
  output out_3
);

  wire xor_1_out;

  xor xor_1 (xor_1_out, BitDoNavio, BitDoTiro);
  not not_1 (out_3, xor_1_out);
endmodule

module Decodificador (
  input  A,
  input  B,
  input  C,
  input  D,
  output SaidaS1,
  output SaidaS2,
  output SaidaS3,
  output SaidaS4
);

  S1 s1_1 (.A(A), .B(B), .C(C), .D(D), .out_5(SaidaS1));
  S2 s2_1 (.A(A), .B(B), .C(C), .D(D), .out_5(SaidaS2));
  S3 s3_1 (.A(A), .B(B), .C(C), .D(D), .out_5(SaidaS3));
  S4 s4_1 (.A(A), .B(B), .C(C), .D(D), .out_5(SaidaS4));
endmodule

module Comparador (
  input  Bit0DoNavio,
  input  Bit0DoTIro,
  input  Bit1DoNavio,
  input  Bit1DoTIro,
  input  Bit2DoNavio,
  input  Bit2DoTIro,
  input  Bit3DoNavio,
  input  Bit3DoTIro,
  output out_9
);

  wire comparadordebit_1_out_3, comparadordebit_2_out_3, comparadordebit_3_out_3, comparadordebit_4_out_3;

  ComparadorDeBit comparadordebit_1 (.BitDoNavio(Bit0DoNavio), .BitDoTiro(Bit0DoTIro), .out_3(comparadordebit_1_out_3));
  ComparadorDeBit comparadordebit_2 (.BitDoNavio(Bit1DoNavio), .BitDoTiro(Bit1DoTIro), .out_3(comparadordebit_2_out_3));
  ComparadorDeBit comparadordebit_3 (.BitDoNavio(Bit2DoNavio), .BitDoTiro(Bit2DoTIro), .out_3(comparadordebit_3_out_3));
  ComparadorDeBit comparadordebit_4 (.BitDoNavio(Bit3DoNavio), .BitDoTiro(Bit3DoTIro), .out_3(comparadordebit_4_out_3));
  and and_1 (out_9, comparadordebit_1_out_3, comparadordebit_2_out_3, comparadordebit_3_out_3, comparadordebit_4_out_3);
endmodule

module Latch (
  input  R,
  input  S,
  output Acertou,
  output Errou
);

  nor nor_1 (Acertou, R, Errou);
  nor nor_2 (Errou, Acertou, S);
endmodule
